// Digital circuit ALU.dig as structural Verilog
module ALU (
  input  [3:0] Entrada,
  input  [7:0] A,
  input  [7:0] B,
  output [7:0] sd
);

  wire somador8bits_1_overflow, sub8_1_bout7;
  wire [7:0] multiplicador_1_saida0, oper_and_1_re, oper_or_1_re, oper_xor_1_re, shift_left_1_left,
       shift_right_1_shift_right, somador8bits_1_saida, sub8_1_saida0;

  oper_AND oper_and_1 (
    .A0(A[0]), .B0(B[0]), .A1(A[1]), .B1(B[1]), .A2(A[2]), .B2(B[2]), .A3(A[3]), .B3(B[3]), .A4(A[4]),
    .B4(B[4]), .A5(A[5]), .B5(B[5]), .A6(A[6]), .B6(B[6]), .A7(A[7]), .B7(B[7]), .Re(oper_and_1_re));
  oper_XOR oper_xor_1 (
    .A0(A[0]), .B0(B[0]), .A1(A[1]), .B1(B[1]), .A2(A[2]), .B2(B[2]), .A3(A[3]), .B3(B[3]), .A4(A[4]),
    .B4(B[4]), .A5(A[5]), .B5(B[5]), .A6(A[6]), .B6(B[6]), .A7(A[7]), .B7(B[7]), .Re(oper_xor_1_re));
  oper_OR oper_or_1 (
    .A0(A[0]), .B0(B[0]), .A1(A[1]), .B1(B[1]), .A2(A[2]), .B2(B[2]), .A3(A[3]), .B3(B[3]), .A4(A[4]),
    .B4(B[4]), .A5(A[5]), .B5(B[5]), .A6(A[6]), .B6(B[6]), .A7(B[7]), .B7(B[7]), .Re(oper_or_1_re));
  Somador8Bits somador8bits_1 (
    .A0(A[0]), .B0(B[0]), .A2(A[2]), .B2(B[2]), .A1(A[1]), .B1(B[1]), .A3(A[3]), .B3(B[3]), .A4(A[4]),
    .B4(B[4]), .A6(A[6]), .B6(B[6]), .A5(A[5]), .B5(B[5]), .A7(A[7]), .B7(B[7]),
    .saida(somador8bits_1_saida), .overflow(somador8bits_1_overflow));
  shift_right shift_right_1 (
    .A0(A[0]), .A1(A[1]), .A2(A[2]), .A3(A[3]), .A4(A[4]), .A5(A[5]), .A6(A[6]), .A7(A[7]),
    .shift_right(shift_right_1_shift_right));
  shift_left shift_left_1 (
    .A0(A[0]), .A1(A[1]), .A2(A[2]), .A3(A[3]), .A4(A[4]), .A5(A[5]), .A6(A[6]), .A7(A[7]),
    .LEFT(shift_left_1_left));
  LED led_1 (.in(somador8bits_1_overflow));
  SUB8 sub8_1 (
    .A0(A[0]), .B0(B[0]), .A1(A[1]), .B1(B[1]), .A2(A[2]), .B2(B[2]), .A3(A[3]), .B3(B[3]), .A4(A[4]),
    .B4(B[4]), .A5(A[5]), .B5(B[5]), .A6(A[6]), .B6(B[6]), .A7(B[7]), .B7(B[7]), .Bout7(sub8_1_bout7),
    .saida0(sub8_1_saida0));
  multiplicador multiplicador_1 (
    .A0(A[0]), .A1(A[1]), .A2(A[2]), .A3(A[3]), .B0(B[0]), .B1(B[1]), .B2(B[2]), .B3(B[3]),
    .saida0(multiplicador_1_saida0));
  LED led_2 (.in(sub8_1_bout7));
  Multiplexer #(.Selector_Bits(4), .Bits(8)) multiplexer_1 (
    .sel(Entrada), .in_0(oper_and_1_re), .in_1(oper_xor_1_re), .in_2(oper_or_1_re),
    .in_3(shift_right_1_shift_right), .in_4(shift_left_1_left), .in_5(somador8bits_1_saida),
    .in_6(sub8_1_saida0), .in_7(multiplicador_1_saida0), .in_8({8{1'b0}}), .in_9({8{1'b0}}),
    .in_10({8{1'b0}}), .in_11({8{1'b0}}), .in_12({8{1'b0}}), .in_13({8{1'b0}}), .in_14({8{1'b0}}),
    .in_15({8{1'b0}}), .out(sd));
  Seven_Seg_Hex seven_seg_hex_1 (.d(sd[3:0]), .dp(1'b0));
endmodule
