// Digital circuit Somador8Bits.dig as structural Verilog
module Somador8Bits (
  input  A0,
  input  B0,
  input  A2,
  input  B2,
  input  A1,
  input  B1,
  input  A3,
  input  B3,
  input  A4,
  input  B4,
  input  A6,
  input  B6,
  input  A5,
  input  B5,
  input  A7,
  input  B7,
  output [7:0] saida,
  output overflow
);

  wire and_1_out, and_2_out, and_3_out, and_4_out, and_5_out, and_6_out, and_7_out, and_8_out, and_9_out,
       and_10_out, and_11_out, and_12_out, and_13_out, and_14_out, and_15_out, and_16_out, and_17_out,
       and_18_out, and_19_out, and_20_out, and_21_out, and_22_out, and_23_out, and_24_out, or_1_out,
       or_2_out, or_3_out, or_4_out, or_5_out, or_6_out, or_7_out, or_8_out, or_9_out, or_10_out, or_11_out,
       or_12_out, or_13_out, or_14_out, or_15_out, xor_1_out, xor_3_out, xor_5_out, xor_7_out, xor_9_out,
       xor_11_out, xor_13_out, xor_15_out;

  LED led1 (.in(A0));
  LED led2 (.in(B0));
  xor xor_1 (xor_1_out, A0, B0);
  and and_1 (and_1_out, A0, B0);
  and and_2 (and_2_out, B0, 1'b0);
  and and_3 (and_3_out, A0, 1'b0);
  LED led9 (.in(A4));
  xor xor_2 (saida[0], xor_1_out, 1'b0);
  LED led10 (.in(B4));
  xor xor_3 (xor_3_out, A4, B4);
  and and_4 (and_4_out, A4, B4);
  and and_5 (and_5_out, B4, or_14_out);
  and and_6 (and_6_out, A4, or_14_out);
  or or_1 (or_1_out, and_1_out, and_2_out);
  xor xor_4 (saida[4], xor_3_out, or_14_out);
  or or_2 (or_2_out, or_1_out, and_3_out);
  or or_3 (or_3_out, and_4_out, and_5_out);
  or or_4 (or_4_out, or_3_out, and_6_out);
  LED led3 (.in(A1));
  xor xor_5 (xor_5_out, A1, B1);
  and and_7 (and_7_out, A1, B1);
  and and_8 (and_8_out, B1, or_2_out);
  and and_9 (and_9_out, A1, or_2_out);
  LED led4 (.in(B1));
  xor xor_6 (saida[1], xor_5_out, or_2_out);
  LED led11 (.in(A5));
  xor xor_7 (xor_7_out, A5, B5);
  and and_10 (and_10_out, A5, B5);
  and and_11 (and_11_out, B5, or_4_out);
  and and_12 (and_12_out, A5, or_4_out);
  or or_5 (or_5_out, and_7_out, and_8_out);
  LED led12 (.in(B5));
  xor xor_8 (saida[5], xor_7_out, or_4_out);
  or or_6 (or_6_out, or_5_out, and_9_out);
  or or_7 (or_7_out, and_10_out, and_11_out);
  or or_8 (or_8_out, or_7_out, and_12_out);
  LED led5 (.in(A2));
  xor xor_9 (xor_9_out, A2, B2);
  and and_13 (and_13_out, A2, B2);
  and and_14 (and_14_out, B2, or_6_out);
  and and_15 (and_15_out, A2, or_6_out);
  LED led6 (.in(B2));
  LED led13 (.in(A6));
  xor xor_10 (saida[2], xor_9_out, or_6_out);
  LED led14 (.in(B6));
  xor xor_11 (xor_11_out, A6, B6);
  and and_16 (and_16_out, A6, B6);
  and and_17 (and_17_out, B6, or_8_out);
  and and_18 (and_18_out, A6, or_8_out);
  or or_9 (or_9_out, and_13_out, and_14_out);
  xor xor_12 (saida[6], xor_11_out, or_8_out);
  or or_10 (or_10_out, or_9_out, and_15_out);
  or or_11 (or_11_out, and_16_out, and_17_out);
  or or_12 (or_12_out, or_11_out, and_18_out);
  LED led7 (.in(B3));
  xor xor_13 (xor_13_out, A3, B3);
  and and_19 (and_19_out, A3, B3);
  and and_20 (and_20_out, B3, or_10_out);
  and and_21 (and_21_out, A3, or_10_out);
  LED led8 (.in(A3));
  xor xor_14 (saida[3], xor_13_out, or_10_out);
  LED led15 (.in(B7));
  xor xor_15 (xor_15_out, A7, B7);
  and and_22 (and_22_out, A7, B7);
  and and_23 (and_23_out, B7, or_12_out);
  and and_24 (and_24_out, A7, or_12_out);
  LED led16 (.in(A7));
  or or_13 (or_13_out, and_19_out, and_20_out);
  xor xor_16 (saida[7], xor_15_out, or_12_out);
  or or_14 (or_14_out, or_13_out, and_21_out);
  or or_15 (or_15_out, and_22_out, and_23_out);
  or or_16 (overflow, or_15_out, and_24_out);

  // Other names for the same wires on the sheet: Sum0 = saida[0]; Sum1 = saida[1]; Sum2 = saida[2]; Sum3 = saida[3];
  //   Sum4 = saida[4]; Sum5 = saida[5]; Sum6 = saida[6]; Sum7 = saida[7]
endmodule
