// Digital circuit multiplicador.dig as structural Verilog
module multiplicador (
  input  A0,
  input  A1,
  input  A2,
  input  A3,
  input  B0,
  input  B1,
  input  B2,
  input  B3,
  output [7:0] saida0
);

  wire and_1_out, and_2_out, and_3_out, and_5_out, and_6_out, and_7_out, and_8_out, and_9_out, and_10_out,
       and_11_out, and_12_out, and_13_out, and_14_out, and_15_out, and_16_out, somador1bit_1_cout0,
       somador1bit_2_cout0, somador1bit_2_sum0, somador1bit_3_cout0, somador1bit_3_sum0, somador1bit_4_cout0,
       somador1bit_4_sum0, somador1bit_5_cout0, somador1bit_5_sum0, somador1bit_6_cout0, somador1bit_7_cout0,
       somador1bit_8_cout0, somador1bit_8_sum0, somador1bit_9_cout0, somador1bit_9_sum0,
       somador1bit_10_cout0, somador1bit_10_sum0, somador1bit_11_cout0, somador1bit_12_cout0,
       somador1bit_13_cout0, somador1bit_14_cout0;

  and and_1 (and_1_out, B0, A3);
  and and_2 (and_2_out, B0, A2);
  and and_3 (and_3_out, B0, A1);
  and and_4 (saida0[0], B0, A0);
  and and_5 (and_5_out, B1, A3);
  and and_6 (and_6_out, B1, A2);
  and and_7 (and_7_out, B1, A1);
  and and_8 (and_8_out, B1, A0);
  and and_9 (and_9_out, B2, A3);
  and and_10 (and_10_out, B2, A2);
  and and_11 (and_11_out, B2, A1);
  and and_12 (and_12_out, B2, A0);
  and and_13 (and_13_out, B3, A3);
  and and_14 (and_14_out, B3, A2);
  and and_15 (and_15_out, B3, A1);
  and and_16 (and_16_out, B3, A0);
  somador1bit somador1bit_1 (
    .A0(and_3_out), .B0(and_8_out), .Cin0(1'b0), .Sum0(saida0[1]), .Cout0(somador1bit_1_cout0));
  somador1bit somador1bit_2 (
    .A0(and_12_out), .B0(and_7_out), .Cin0(1'b0), .Sum0(somador1bit_2_sum0), .Cout0(somador1bit_2_cout0));
  somador1bit somador1bit_3 (
    .A0(and_1_out), .B0(and_6_out), .Cin0(1'b0), .Sum0(somador1bit_3_sum0), .Cout0(somador1bit_3_cout0));
  somador1bit somador1bit_4 (
    .A0(and_5_out), .B0(and_10_out), .Cin0(1'b0), .Sum0(somador1bit_4_sum0), .Cout0(somador1bit_4_cout0));
  somador1bit somador1bit_5 (
    .A0(and_9_out), .B0(and_14_out), .Cin0(1'b0), .Sum0(somador1bit_5_sum0), .Cout0(somador1bit_5_cout0));
  somador1bit somador1bit_6 (
    .A0(and_13_out), .B0(1'b0), .Cin0(somador1bit_13_cout0), .Sum0(saida0[6]), .Cout0(somador1bit_6_cout0));
  somador1bit somador1bit_7 (
    .A0(somador1bit_2_sum0), .B0(and_2_out), .Cin0(somador1bit_1_cout0), .Sum0(saida0[2]),
    .Cout0(somador1bit_7_cout0));
  somador1bit somador1bit_8 (
    .A0(somador1bit_3_sum0), .B0(and_11_out), .Cin0(somador1bit_3_cout0), .Sum0(somador1bit_8_sum0),
    .Cout0(somador1bit_8_cout0));
  somador1bit somador1bit_9 (
    .A0(somador1bit_4_sum0), .B0(and_15_out), .Cin0(somador1bit_4_cout0), .Sum0(somador1bit_9_sum0),
    .Cout0(somador1bit_9_cout0));
  somador1bit somador1bit_10 (
    .A0(somador1bit_5_sum0), .B0(1'b0), .Cin0(somador1bit_5_cout0), .Sum0(somador1bit_10_sum0),
    .Cout0(somador1bit_10_cout0));
  somador1bit somador1bit_11 (
    .A0(somador1bit_8_sum0), .B0(and_16_out), .Cin0(somador1bit_7_cout0), .Sum0(saida0[3]),
    .Cout0(somador1bit_11_cout0));
  somador1bit somador1bit_12 (
    .A0(somador1bit_9_sum0), .B0(1'b0), .Cin0(somador1bit_11_cout0), .Sum0(saida0[4]),
    .Cout0(somador1bit_12_cout0));
  somador1bit somador1bit_13 (
    .A0(somador1bit_10_sum0), .B0(1'b0), .Cin0(somador1bit_12_cout0), .Sum0(saida0[5]),
    .Cout0(somador1bit_13_cout0));
  somador1bit somador1bit_14 (
    .A0(1'b0), .B0(1'b0), .Cin0(somador1bit_6_cout0), .Sum0(saida0[7]), .Cout0(somador1bit_14_cout0));
  LED led_1 (.in(somador1bit_14_cout0));
  // also tied to GND on the sheet: {somador1bit_2_cout0, somador1bit_8_cout0, somador1bit_9_cout0, somador1bit_10_cout0}

  // Other names for the same wires on the sheet: P0 = saida0[0]; P1 = saida0[1]; P2 = saida0[2]; P3 = saida0[3];
  //   P4 = saida0[4]; P5 = saida0[5]; P6 = saida0[6]; P7 = saida0[7]
endmodule
