// Digital circuit oper_XOR.dig as structural Verilog
module oper_XOR (
  input  A0,
  input  B0,
  input  A1,
  input  B1,
  input  A2,
  input  B2,
  input  A3,
  input  B3,
  input  A4,
  input  B4,
  input  A5,
  input  B5,
  input  A6,
  input  B6,
  input  A7,
  input  B7,
  output [7:0] Re
);

  xor xor_1 (Re[0], A0, B0);
  xor xor_2 (Re[1], A1, B1);
  xor xor_3 (Re[2], A2, B2);
  xor xor_4 (Re[3], A3, B3);
  xor xor_5 (Re[4], A4, B4);
  xor xor_6 (Re[5], A5, B5);
  xor xor_7 (Re[6], A6, B6);
  xor xor_8 (Re[7], A7, B7);
endmodule
