// Digital circuit shift_right.dig as structural Verilog
module shift_right (
  input  A0,
  input  A1,
  input  A2,
  input  A3,
  input  A4,
  input  A5,
  input  A6,
  input  A7,
  output [7:0] shift_right
);


  assign shift_right = {A7, A6, A5, A4, A3, A2, A1, A0};
endmodule
