// Digital circuit SUB8.dig as structural Verilog
module SUB8 (
  input  A0,
  input  B0,
  input  A1,
  input  B1,
  input  A2,
  input  B2,
  input  A3,
  input  B3,
  input  A4,
  input  B4,
  input  A5,
  input  B5,
  input  A6,
  input  B6,
  input  A7,
  input  B7,
  output Bout7,
  output [7:0] saida0
);

  wire sub0_bout, sub1_bout, sub2_bout, sub3_bout, sub4_bout, sub5_bout, sub6_bout;

  subtrator1bit sub0 (.A(A0), .B(B0), .BIn(1'b0), .D(saida0[0]), .Bout(sub0_bout));
  subtrator1bit sub1 (.A(A1), .B(B1), .BIn(sub0_bout), .D(saida0[1]), .Bout(sub1_bout));
  subtrator1bit sub2 (.A(A2), .B(B2), .BIn(sub1_bout), .D(saida0[2]), .Bout(sub2_bout));
  subtrator1bit sub3 (.A(A3), .B(B3), .BIn(sub2_bout), .D(saida0[3]), .Bout(sub3_bout));
  subtrator1bit sub4 (.A(A4), .B(B4), .BIn(sub3_bout), .D(saida0[4]), .Bout(sub4_bout));
  subtrator1bit sub5 (.A(A5), .B(B5), .BIn(sub4_bout), .D(saida0[5]), .Bout(sub5_bout));
  subtrator1bit sub6 (.A(A6), .B(B6), .BIn(sub5_bout), .D(saida0[6]), .Bout(sub6_bout));
  subtrator1bit sub7 (.A(A7), .B(B7), .BIn(sub6_bout), .D(saida0[7]), .Bout(Bout7));

  // Other names for the same wires on the sheet: D0 = saida0[0]; D1 = saida0[1]; D2 = saida0[2]; D3 = saida0[3];
  //   D4 = saida0[4]; D5 = saida0[5]; D6 = saida0[6]; D7 = saida0[7]
endmodule
