// Digital circuit cpu.dig as structural Verilog
module cpu (
  input  [3:0] pc
);

  wire \botão_para_clock_out ;
  wire [7:0] alu_1_sd, register_1_q;
  wire [11:0] eepromdualport_1_d;

  EEPROMDualPort #(.AddrBits(4), .Bits(12)) eepromdualport_1 (
    .A(pc), .Din({12{1'b0}}), .str(1'b0), .C(\botão_para_clock_out ), .ld(1'b1), .D(eepromdualport_1_d));
  Button \botão_para_clock  (.out(\botão_para_clock_out ));
  ALU alu_1 (.Entrada(eepromdualport_1_d[3:0]), .A(eepromdualport_1_d[11:4]), .B(register_1_q), .sd(alu_1_sd));
  Register #(.Bits(8)) register_1 (.D(alu_1_sd), .C(\botão_para_clock_out ), .en(1'b1), .Q(register_1_q));
  Seven_Seg_Hex seven_seg_hex_1 (.d(register_1_q[7:4]), .dp(1'b0));
  Seven_Seg_Hex seven_seg_hex_2 (.d(register_1_q[3:0]), .dp(1'b0));

  // Notes on the sheet:
  //   contents of eepromdualport_1 (hex, n*v repeats v):
  //   53,33,23,14
endmodule
