// Digital circuit shift_left.dig as structural Verilog
module shift_left (
  input  A0,
  input  A1,
  input  A2,
  input  A3,
  input  A4,
  input  A5,
  input  A6,
  input  A7,
  output [7:0] LEFT
);


  assign LEFT = {A7, A6, A5, A4, A3, A2, A1, A0};
endmodule
