// Digital circuit somador1bit.dig as structural Verilog
module somador1bit (
  input  A0,
  input  B0,
  input  Cin0,
  output Sum0,
  output Cout0
);

  wire and_1_out, and_2_out, and_3_out, or_1_out, xor_1_out;

  LED led1 (.in(A0));
  xor xor_1 (xor_1_out, A0, B0);
  and and_1 (and_1_out, A0, B0);
  and and_2 (and_2_out, B0, Cin0);
  and and_3 (and_3_out, A0, Cin0);
  LED led2 (.in(B0));
  xor xor_2 (Sum0, xor_1_out, Cin0);
  or or_1 (or_1_out, and_1_out, and_2_out);
  or or_2 (Cout0, or_1_out, and_3_out);
endmodule
