// Digital circuit subtrator1bit.dig as structural Verilog
module subtrator1bit (
  input  A,
  input  B,
  input  BIn,
  output D,
  output Bout
);

  wire and_1_out, and_2_out, not_1_out, not_2_out, xor_1_out;

  xor xor_1 (xor_1_out, B, BIn);
  not not_1 (not_1_out, B);
  and and_1 (and_1_out, not_1_out, BIn);
  xor xor_2 (D, A, xor_1_out);
  not not_2 (not_2_out, xor_1_out);
  and and_2 (and_2_out, not_2_out, A);
  or or_1 (Bout, and_2_out, and_1_out);

  // Notes on the sheet:
  //   BIn: bit de empréstimo de entrada
endmodule
